// Logisim project s-mips.circ as structural Verilog: 68 circuits, main circuit S-MIPS Board
module S_MIPS_Board (
  input  DESHABILITAR_DISPATCHER,
  output halt
);

  wire button_1_out, CLK, CS, d_ff_1_q, LCLR, LoadRAM, LoadRAMOn, LW, R_R_W, R_W, ram_dispatcher_1_finished,
       RCS, Reset_out, RST, TTY_EN;
  wire [2:0] KDB;
  wire [3:0] LMask, Mask, ram_1_read_time, ram_1_write_time, RMask;
  wire [6:0] KDB_DATA, TTY_DATA;
  wire [15:0] Addr, LAddr, RAddr;
  wire [31:0] I0, I1, I2, I3, LData, ram_1_data_out_0, ram_1_data_out_1, ram_1_data_out_2, ram_1_data_out_3,
       RI0, RI1, RI2, RI3;

  TTY #(.rows(25), .cols(100)) tty_1 (.data(TTY_DATA), .clk(CLK), .we(TTY_EN), .clr(RST));
  not not_1 (LoadRAMOn, ram_dispatcher_1_finished);
  RAM_Dispatcher ram_dispatcher_1 (
    .WriteTime(ram_1_write_time), .Clock(CLK), .Data(LData), .Address(LAddr), .Mask(LMask),
    .Finished(ram_dispatcher_1_finished), .Write(LW), .CLR(LCLR));
  Keyboard #(.buflen(64)) keyboard_1 (.clk(CLK), .re(KDB[0]), .avail(KDB[2]), .data(KDB_DATA));  // open: clr
  RAM ram_1 (
    .Address(RAddr), .Data_Out_0(ram_1_data_out_0), .Data_Out_1(ram_1_data_out_1),
    .Data_Out_2(ram_1_data_out_2), .Data_Out_3(ram_1_data_out_3), .Data_In_0(RI0), .Data_In_1(RI1),
    .Data_In_2(RI2), .Data_In_3(RI3), .Mask(RMask), .nRead_Write(R_R_W), .Chip_Select(RCS),
    .Read_Time(ram_1_read_time), .Reset(button_1_out), .Write_Time(ram_1_write_time));
  Button button_1 (.out(button_1_out));
  D_Flip_Flop d_ff_1 (.clk(CLK), .D(1'b1), .Q(d_ff_1_q), .reset(Reset_out));  // open: Qn, preset, en
  Button Reset (.out(Reset_out));
  S_MIPS s_mips_1 (
    .Kbd_Enable(KDB[0]), .Address(Addr), .Kbd_Clear(KDB[1]), .Kbd_Available(KDB[2]),
    .Kbd_ASCII_Data(KDB_DATA), .RAM_Out_0(ram_1_data_out_0), .TTY_Enable(TTY_EN),
    .RAM_Out_1(ram_1_data_out_1), .TTY_ASCII_Data(TTY_DATA), .Reset(RST), .RAM_Out_2(ram_1_data_out_2),
    .Stop(halt), .RAM_Out_3(ram_1_data_out_3), .RAM_In_0(I0), .RAM_In_1(I1), .RAM_In_2(I2), .RAM_In_3(I3),
    .Mask(Mask), .Read_Time(ram_1_read_time), .Write_Time(ram_1_write_time), .nRead_Write(R_W),
    .Chip_Select(CS), .Clock(CLK));
  D_Flip_Flop d_ff_2 (.clk(CLK), .D(d_ff_1_q), .Qn(LCLR), .reset(Reset_out));  // open: Q, preset, en
  or or_1 (RST, LCLR, LoadRAM);
  Clock clock_1 (.out(CLK));
  Multiplexer #(.width(32), .enable("false")) multiplexer_1 (.in0(I0), .in1(LData), .out(RI0), .sel(LoadRAM));
  Multiplexer #(.width(32), .enable("false")) multiplexer_2 (.in0(I1), .in1(LData), .out(RI1), .sel(LoadRAM));
  Multiplexer #(.width(32), .enable("false")) multiplexer_3 (.in0(I2), .in1(LData), .out(RI2), .sel(LoadRAM));
  Multiplexer #(.width(32), .enable("false")) multiplexer_4 (.in0(I3), .in1(LData), .out(RI3), .sel(LoadRAM));
  and and_1 (LoadRAM, ~DESHABILITAR_DISPATCHER, LoadRAMOn);  // AND_Gate
  Multiplexer #(.width(16), .enable("false")) multiplexer_5 (.in0(Addr), .in1(LAddr), .out(RAddr), .sel(LoadRAM));
  Multiplexer #(.width(4), .enable("false")) multiplexer_6 (.in0(Mask), .in1(LMask), .out(RMask), .sel(LoadRAM));
  Multiplexer #(.enable("false")) multiplexer_7 (.in0(CS), .in1(LW), .out(RCS), .sel(LoadRAM));
  Multiplexer #(.enable("false")) multiplexer_8 (.in0(R_W), .in1(LW), .out(R_R_W), .sel(LoadRAM));

  // Notes on the sheet:
  //   NO MODIFICAR
  //   Keyboard
endmodule

module RAM (
  input  [15:0] Address,
  input  [31:0] Data_In_0,
  input  [31:0] Data_In_1,
  input  [31:0] Data_In_2,
  input  [31:0] Data_In_3,
  input  [3:0] Mask,
  input  nRead_Write,
  input  Chip_Select,
  input  Reset,
  output [31:0] Data_Out_0,
  output [31:0] Data_Out_1,
  output [31:0] Data_Out_2,
  output [31:0] Data_Out_3,
  output [3:0] Read_Time,
  output [3:0] Write_Time
);

  wire and_2_out, and_3_out, and_4_out, and_5_out, and_6_out, and_7_out, and_8_out, and_9_out, Changed, CLK,
       comparator_2_eq, comparator_3_eq, comparator_4_eq, comparator_5_eq, comparator_6_eq, Count,
       demultiplexer_3_out0, Idle, Idle_q, Load, Load0, Load1, nand_1_out, or_1_out, or_2_out, or_3_out,
       or_4_out, or_5_out, or_6_out, or_7_out, or_8_out, or_9_out, or_10_out, Proc_q, Update_Mem, Zero_Time;
  wire [3:0] counter_1_q, multiplexer_1_out, subtractor_1_out;
  wire [31:0] register_1_q, register_2_q, register_3_q, register_4_q, register_5_q;

  // Probe on 4'b0011
  // Probe on 4'b0010
  Multiplexer #(.width(4), .enable("false")) multiplexer_1 (
    .in0(4'b0011), .in1(4'b0010), .out(multiplexer_1_out), .sel(nRead_Write));
  or or_1 (or_1_out, Idle, Update_Mem);
  or or_2 (or_2_out, ~Chip_Select, Reset);  // OR_Gate
  Subtractor #(.width(4)) subtractor_1 (.a(multiplexer_1_out), .b(4'b0010), .out(subtractor_1_out));  // open: bin, bout
  Demultiplexer #(.enable("false")) demultiplexer_1 (.out0(Idle), .out1(Load0), .in(Idle_q), .sel(Changed));
  D_Flip_Flop u_Idle (.clk(CLK), .D(or_1_out), .Q(Idle_q), .preset(or_2_out));  // open: Qn, en, reset
  // Probe on counter_1_q
  Counter #(.width(4), .max('hf)) counter_1 (
    .load(Load), .D(subtractor_1_out), .count(Count), .Q(counter_1_q), .clk(CLK), .clr(or_3_out));  // open: carry
  or or_3 (or_3_out, ~Chip_Select, Reset);  // OR_Gate
  Comparator #(.width(4), .mode("unsigned")) comparator_1 (
    .a(4'b0000), .b(counter_1_q), .eq(Zero_Time));  // open: gt, lt
  or or_4 (or_4_out, Count, Load0, Load1);
  Register #(.width(32)) register_1 (.D(Data_In_0), .en(Chip_Select), .Q(register_1_q), .clk(CLK), .clr(or_5_out));
  or or_5 (or_5_out, ~Chip_Select, Reset);  // OR_Gate
  Register #(.width(32)) register_2 (.D(Data_In_1), .en(Chip_Select), .Q(register_2_q), .clk(CLK), .clr(or_6_out));
  or or_6 (or_6_out, ~Chip_Select, Reset);  // OR_Gate
  Register #(.width(32)) register_3 (.D(Data_In_2), .en(Chip_Select), .Q(register_3_q), .clk(CLK), .clr(or_7_out));
  or or_7 (or_7_out, ~Chip_Select, Reset);  // OR_Gate
  Register #(.width(32)) register_4 (.D(Data_In_3), .en(Chip_Select), .Q(register_4_q), .clk(CLK), .clr(or_8_out));
  or or_8 (or_8_out, ~Chip_Select, Reset);  // OR_Gate
  Register #(.width(32)) register_5 (
    .D({{11{1'b1}}, nRead_Write, Mask, Address}), .en(Chip_Select), .Q(register_5_q), .clk(CLK),
    .clr(or_9_out));
  or or_9 (or_9_out, ~Chip_Select, Reset);  // OR_Gate
  D_Flip_Flop Proc (.clk(CLK), .D(or_4_out), .Q(Proc_q), .reset(or_10_out));  // open: Qn, preset, en
  or or_10 (or_10_out, ~Chip_Select, Reset);  // OR_Gate
  Demultiplexer #(.enable("false")) demultiplexer_2 (
    .out0(Count), .out1(Update_Mem), .in(demultiplexer_3_out0), .sel(Zero_Time));
  Demultiplexer #(.enable("false")) demultiplexer_3 (
    .out0(demultiplexer_3_out0), .out1(Load1), .in(Proc_q), .sel(Changed));
  Clock clock_1 (.out(CLK));
  Comparator #(.width(32)) comparator_2 (.a(register_1_q), .b(Data_In_0), .eq(comparator_2_eq));  // open: gt, lt
  Comparator #(.width(32)) comparator_3 (.a(register_2_q), .b(Data_In_1), .eq(comparator_3_eq));  // open: gt, lt
  Comparator #(.width(32)) comparator_4 (.a(register_3_q), .b(Data_In_2), .eq(comparator_4_eq));  // open: gt, lt
  Comparator #(.width(32)) comparator_5 (.a(register_4_q), .b(Data_In_3), .eq(comparator_5_eq));  // open: gt, lt
  Comparator #(.width(32)) comparator_6 (
    .a(register_5_q), .b({{11{1'b1}}, nRead_Write, Mask, Address}), .eq(comparator_6_eq));  // open: gt, lt
  nand nand_1 (nand_1_out, comparator_6_eq, comparator_2_eq, comparator_3_eq, comparator_4_eq, comparator_5_eq);
  and and_1 (Changed, nand_1_out, Chip_Select);
  or or_11 (Load, Count, Load1, Load0);
  and and_2 (and_2_out, Mask[0], Update_Mem, nRead_Write);
  and and_3 (and_3_out, Mask[1], Update_Mem, nRead_Write);
  and and_4 (and_4_out, Mask[2], Update_Mem, nRead_Write);
  and and_5 (and_5_out, Mask[3], Update_Mem, nRead_Write);
  RAM_part #(.addrWidth(16), .dataWidth(32), .bus("separate")) ram_1 (
    .addr(Address), .din(Data_In_0), .data(Data_Out_0), .str(and_2_out), .sel(Chip_Select), .clk(CLK),
    .ld(and_6_out), .clr(Reset));
  and and_6 (and_6_out, ~nRead_Write, Idle);  // AND_Gate
  RAM_part #(.addrWidth(16), .dataWidth(32), .bus("separate")) ram_2 (
    .addr(Address), .din(Data_In_1), .data(Data_Out_1), .str(and_3_out), .sel(Chip_Select), .clk(CLK),
    .ld(and_7_out), .clr(Reset));
  and and_7 (and_7_out, ~nRead_Write, Idle);  // AND_Gate
  RAM_part #(.addrWidth(16), .dataWidth(32), .bus("separate")) ram_3 (
    .addr(Address), .din(Data_In_2), .data(Data_Out_2), .str(and_4_out), .sel(Chip_Select), .clk(CLK),
    .ld(and_8_out), .clr(Reset));
  and and_8 (and_8_out, ~nRead_Write, Idle);  // AND_Gate
  RAM_part #(.addrWidth(16), .dataWidth(32), .bus("separate")) ram_4 (
    .addr(Address), .din(Data_In_3), .data(Data_Out_3), .str(and_5_out), .sel(Chip_Select), .clk(CLK),
    .ld(and_9_out), .clr(Reset));
  and and_9 (and_9_out, ~nRead_Write, Idle);  // AND_Gate

  assign Read_Time = 4'b0011;
  assign Write_Time = 4'b0010;

  // Other names for the same wires on the sheet: M0 = Mask[0]; M1 = Mask[1]; M2 = Mask[2]; M3 = Mask[3];
  //   RW = nRead_Write; CLR = Reset; CS = Chip_Select; Load2 = Count

  // Notes on the sheet:
  //   NO MODIFICAR
  //   excepto quizás los valores RT y WT
  //   BANK0
  //   BANK1
  //   BANK2
  //   BANK3
endmodule

module S_MIPS (
  input  Kbd_Available,
  input  [6:0] Kbd_ASCII_Data,
  input  [31:0] RAM_Out_0,
  input  [31:0] RAM_Out_1,
  input  Reset,
  input  [31:0] RAM_Out_2,
  input  Clock,
  input  [31:0] RAM_Out_3,
  input  [3:0] Read_Time,
  input  [3:0] Write_Time,
  output Kbd_Enable,
  output [15:0] Address,
  output Kbd_Clear,
  output TTY_Enable,
  output [6:0] TTY_ASCII_Data,
  output Stop,
  output [31:0] RAM_In_0,
  output [31:0] RAM_In_1,
  output [31:0] RAM_In_2,
  output [31:0] RAM_In_3,
  output [3:0] Mask,
  output nRead_Write,
  output Chip_Select
);

  wire and_1_out, comparator_3_eq, counter_1_q, D, Jmp, M, push_bool_1_output, R, R_minus, R_W, S_Div,
       S_Mult, sw_bool_1_output;
  wire [1:0] P;
  wire [3:0] counter_2_q, counter_3_q, Time;
  wire [4:0] DA, SA, SB;
  wire [5:0] multiplexer_6_out;
  wire [15:0] Constant;
  wire [26:0] multiplexer_7_out;
  wire [31:0] A, adder_1_out, B, Inst, inversor_1_out_2, multiplexer_1_out, multiplexer_2_out,
       multiplexer_4_out, Op, Out, Pc, PC_prime, register_1_q;

  Register #(.width(32), .trigger("falling")) register_1 (
    .D({Pc[31:4], P, Pc[1:0]}), .Q({register_1_q[31:20], Address, register_1_q[3:0]}), .clk(Clock),
    .clr(Reset));  // open: en
  Adder #(.width(32)) adder_1 (.a(32'h4), .b({Pc[31:4], P, Pc[1:0]}), .out(adder_1_out));  // open: cin, cout
  and and_1 (and_1_out, Clock, D);
  Demultiplexer #(.select(2), .width(32), .enable("false")) demultiplexer_1 (
    .out0(RAM_In_0), .out1(RAM_In_1), .out2(RAM_In_2), .out3(RAM_In_3), .in(Out), .sel(P));
  // Probe on multiplexer_1_out
  Multiplexer #(.width(32), .enable("false")) multiplexer_1 (
    .in0({32{1'b0}}), .in1(multiplexer_2_out), .out(multiplexer_1_out), .sel(counter_1_q));
  Multiplexer #(.width(32), .enable("false")) multiplexer_2 (
    .in0(adder_1_out), .in1(PC_prime), .out(multiplexer_2_out), .sel(Jmp));
  Counter #(.width(1), .max('h1), .ongoal("stay"), .trigger("falling")) counter_1 (
    .Q(counter_1_q), .clk(and_1_out));  // open: load, D, count, carry, clr
  Decoder #(.select(2), .enable("false")) decoder_1 (
    .out0(Mask[0]), .out1(Mask[1]), .out2(Mask[2]), .out3(Mask[3]), .sel(P));
  Register #(.width(32)) register_2 (
    .D(multiplexer_1_out), .en(R_minus), .Q({Pc[31:4], P, Pc[1:0]}), .clk(Clock), .clr(Reset));
  Counter #(.width(4), .max('hf)) counter_2 (.Q(counter_2_q), .clk(and_1_out), .clr(R));  // open: load, D, count, carry
  // Probe on {Pc[31:4], P, Pc[1:0]}
  Comparator #(.width(4), .mode("unsigned")) comparator_1 (.a(counter_2_q), .b(4'b0101), .eq(R_minus));  // open: gt, lt
  Comparator #(.width(4), .mode("unsigned")) comparator_2 (.a(counter_2_q), .b(4'b0110), .eq(R));  // open: gt, lt
  Counter #(.width(4), .max('hf)) counter_3 (.Q(counter_3_q), .clk(Clock), .clr(R));  // open: load, D, count, carry
  Counter #(.width(1), .max('h1), .ongoal("stay")) counter_4 (
    .Q(D), .clk(comparator_3_eq), .clr(R));  // open: load, D, count, carry
  Comparator #(.width(4)) comparator_3 (.a(Time), .b(counter_3_q), .eq(comparator_3_eq));  // open: gt, lt
  Multiplexer #(.width(4), .enable("false")) multiplexer_3 (
    .in0(Read_Time), .in1(Write_Time), .out(Time), .sel(nRead_Write));
  // Probe on multiplexer_4_out
  Multiplexer #(.width(32), .enable("false")) multiplexer_4 (
    .in0({32{1'b0}}), .in1(Inst), .out(multiplexer_4_out), .sel(D));
  // Probe on inversor_1_out_2
  Inversor inversor_1 (.in_1(multiplexer_4_out), .out_2(inversor_1_out_2));
  Branch_Control branch_control_1 (
    .Js(Constant), .Pc({Pc[31:4], P, Pc[1:0]}), .PC_prime(PC_prime), .Op(Op), .A(A), .B(B), .Inst(Inst),
    .Clock(Clock), .Jump(Jmp));
  Multiplexer #(.select(2), .width(32), .enable("false")) multiplexer_5 (
    .in0(RAM_Out_0), .in1(RAM_Out_1), .in2(RAM_Out_2), .in3(RAM_Out_3), .out(Inst), .sel(P));
  // Probe on P
  Instruction_Decoder instruction_decoder_1 (
    .W_Id(nRead_Write), .Op(Op), .S_Mult(S_Mult), .S_Div(S_Div), .SA(SA), .SB(SB),
    .Instruction(inversor_1_out_2), .Jmp(Jmp), .R___W(R_W), .Data_Address(DA), .Constant(Constant), .Memory(M));
  // Probe on Inst
  Sw_Bool sw_bool_1 (.Input(multiplexer_6_out), .Output(sw_bool_1_output));
  Multiplexer #(.width(6), .enable("false")) multiplexer_6 (
    .in0({6{1'b0}}), .in1(Inst[31:26]), .out(multiplexer_6_out), .sel(D));
  Push_Bool push_bool_1 (.Input(multiplexer_7_out), .Output(push_bool_1_output));
  Multiplexer #(.width(27), .enable("false")) multiplexer_7 (
    .in0({27{1'b0}}), .in1({Inst[31:26], Inst[20:0]}), .out(multiplexer_7_out), .sel(D));
  // Probe on Out
  Data_Path data_path_1 (
    .Clock(Clock), .RW(R_W), .DA(DA), .Rst(Reset), .SA(SA), .SB(SB), .Op(Op), .Constant(Constant),
    .Output(Out), .A(A), .B(B), .Inst(Inst));
  or or_1 (nRead_Write, sw_bool_1_output, push_bool_1_output);

  assign Chip_Select = 1'b1;
  assign Kbd_Clear = 1'b0;
  assign Kbd_Enable = 1'b0;
  assign Stop = 1'b0;
  assign TTY_ASCII_Data = {7{1'b0}};
  assign TTY_Enable = 1'b0;

  // Other names for the same wires on the sheet: ADDR[15:0] = Address; CLK1 = Clock; KBD_AVAIL = Kbd_Available;
  //   KBD_DATA[6:0] = Kbd_ASCII_Data; Pc[3:2] = P; R1I[31:0] = RAM_In_0; R1O[31:0] = RAM_Out_0; R2I[31:0] = RAM_In_1;
  //   R2O[31:0] = RAM_Out_1; R3I[31:0] = RAM_In_2; R3O[31:0] = RAM_Out_2; R4I[31:0] = RAM_In_3; R4O[31:0] = RAM_Out_3;
  //   RAM_MASK[3:0] = Mask; Rst = Reset; W_Id = nRead_Write

  // Notes on the sheet:
  //   RAM ADDRESS
  //   DATA FROM RAM
  //   DATA TO RAM
  //   DATA WRITE MASK
  //   RAM TIMING
  //   RAM CONTROL
  //   guardar para que verifique con los cambios
  //   Al cambiar de banco tengo que volver a contar RT + WT tiempos
  //   Solo tocar el Rst del Micro no el de la Ram
  //   el mask y los out tienen que estar conectados para que devuelva la ram
  //   KEYBOARD
  //   TTY
  //   SEQUENCING
  //   Program Counter
  //   Address
  //   Write
  //   Output
  //   Time Counter
  //   Branch Control
  //   Logic-Operations
  //   Read
endmodule

module S_MIPS_old (
  input  [15:0] Address,
  input  Kbd_Available,
  input  [6:0] Kbd_ASCII_Data,
  input  [31:0] RAM_Out_0,
  input  [31:0] RAM_Out_1,
  input  Reset,
  input  [31:0] RAM_Out_2,
  input  [31:0] RAM_Out_3,
  input  [31:0] RAM_In_0,
  input  [31:0] RAM_In_1,
  input  [31:0] RAM_In_2,
  input  [31:0] RAM_In_3,
  input  [3:0] Read_Time,
  input  [3:0] Write_Time,
  output Kbd_Enable,
  output Kbd_Clear,
  output TTY_Enable,
  output [6:0] TTY_ASCII_Data,
  output Stop,
  output [3:0] Mask,
  output nRead_Write,
  output Chip_Select
);

  wire Activation_Time_1, Activation_Time_2, Clock_1, Clock_2, instruction_decoder_1_p5,
       instruction_decoder_1_p6, instruction_decoder_1_p7, instruction_decoder_1_p8,
       instruction_decoder_1_p9, instruction_decoder_1_p10, instruction_decoder_1_p11,
       instruction_decoder_1_p12, Jmp;
  wire [3:0] counter_1_q, counter_2_q;
  wire [31:0] ADDR, Inst, PC, Pc_prime, Pc_prime_prime, Result;

  assign ADDR = {{16{1'b0}}, Address};  // Bit_Extender bit_extender_1
  Demultiplexer #(.select(2), .width(32)) demultiplexer_1 (
    .out0(RAM_Out_0), .out1(RAM_Out_1), .out2(RAM_Out_2), .out3(RAM_Out_3), .in(Result), .sel(PC[3:2]));  // open: en
  Multiplexer #(.select(2), .width(32)) multiplexer_1 (
    .in0(RAM_In_0), .in1(RAM_In_1), .in2(RAM_In_2), .in3(RAM_In_3), .out(Inst), .sel(PC[3:2]));  // open: en
  Counter #(.width(4), .max('hf)) counter_1 (.Q(counter_1_q), .clk(Clock_1));  // open: load, D, count, carry, clr
  Counter #(.width(4), .max('hf)) counter_2 (.Q(counter_2_q), .clk(Clock_2));  // open: load, D, count, carry, clr
  PC_3_0 pc_3_0_1 (
    .Clock_1(Activation_Time_1), .Clock_2(Activation_Time_2), .Rst(Reset), .ADDR(ADDR),
    .PC_prime_input(Pc_prime), .PC(PC), .PC_prime(Pc_prime_prime), .Jmp(Jmp));
  Clock u_clock_1 (.out(Clock_1));
  Clock u_clock_2 (.out(Clock_2));
  // Probe on counter_1_q
  Comparator #(.width(4)) comparator_1 (.a(counter_1_q), .b(Read_Time), .eq(Activation_Time_1));  // open: gt, lt
  // Probe on counter_2_q
  Comparator #(.width(4)) comparator_2 (.a(counter_2_q), .b(Write_Time), .eq(Activation_Time_2));  // open: gt, lt
  // Probe on PC
  // Instruction_Decoder instruction_decoder_1: pin names not known; wires that end beside it: Inst, nRead_Write, Reset, PC, instruction_decoder_1_p5, instruction_decoder_1_p6, instruction_decoder_1_p7, instruction_decoder_1_p8, instruction_decoder_1_p9, instruction_decoder_1_p10, instruction_decoder_1_p11, instruction_decoder_1_p12, Jmp
  // Probe on PC[3:2]
  // Data_Path data_path_1: pin names not known; wires that end beside it: instruction_decoder_1_p8, instruction_decoder_1_p9, instruction_decoder_1_p10, instruction_decoder_1_p6, instruction_decoder_1_p7, instruction_decoder_1_p5, instruction_decoder_1_p11, instruction_decoder_1_p12, Result, Pc_prime

  // Other names for the same wires on the sheet: CS = Chip_Select; KBD_AVAIL = Kbd_Available; KBD_CLR = Kbd_Clear;
  //   KBD_DATA[6:0] = Kbd_ASCII_Data; PC_value[1:0] = PC[3:2]; R1I[31:0] = RAM_In_0; R1O[31:0] = RAM_Out_0;
  //   R2I[31:0] = RAM_In_1; R2O[31:0] = RAM_Out_1; R3I[31:0] = RAM_In_2; R3O[31:0] = RAM_Out_2; R4I[31:0] = RAM_In_3;
  //   R4O[31:0] = RAM_Out_3; RAM_MASK[3:0] = Mask; Rst = Reset; TTY_DATA[6:0] = TTY_ASCII_Data; W_Id = nRead_Write

  // Notes on the sheet:
  //   RAM ADDRESS
  //   DATA FROM RAM
  //   DATA TO RAM
  //   DATA WRITE MASK
  //   RAM TIMING
  //   RAM CONTROL
  //   CU
  //   PC
  //   Timer Reader
  //   ID
  //   Data Path
  //   KEYBOARD
  //   TTY
  //   SEQUENCING
endmodule

module RAM_Dispatcher (
  input  [3:0] WriteTime,
  input  Clock,
  input  CLR,
  output [31:0] Data,
  output [15:0] Address,
  output [3:0] Mask,
  output Finished,
  output Write
);

  wire demultiplexer_2_out1, demultiplexer_3_out1, End, IDLE_q, IncAddr, Load, or_1_out, or_2_out, While_q,
       WriteEnd;
  wire [3:0] counter_1_q;
  wire [31:0] CurrentAddress_q;

  Counter #(.width(32), .max('hffffffff)) CurrentAddress (
    .count(IncAddr), .Q({CurrentAddress_q[31:18], Address, CurrentAddress_q[1:0]}), .clk(Clock), .clr(CLR));  // open: load, D, carry
  or or_1 (or_1_out, IncAddr, demultiplexer_3_out1, Finished);
  D_Flip_Flop IDLE (.clk(Clock), .D(or_1_out), .Q(IDLE_q), .preset(CLR));  // open: Qn, en, reset
  Demultiplexer #(.enable("false")) demultiplexer_1 (.out0(Load), .out1(Finished), .in(IDLE_q), .sel(End));
  D_Flip_Flop While (.clk(Clock), .D(or_2_out), .Q(While_q), .reset(CLR));  // open: Qn, preset, en
  or or_2 (or_2_out, Write, Load);
  RAM_part #(.addrWidth(18), .dataWidth(32)) ram_1 (
    .addr({Address, CurrentAddress_q[1:0]}), .data(Data), .clk(Clock));  // open: sel, ld, clr
  Demultiplexer #(.enable("false")) demultiplexer_2 (
    .out0(Write), .out1(demultiplexer_2_out1), .in(While_q), .sel(WriteEnd));
  Decoder #(.select(2)) decoder_1 (
    .out0(Mask[0]), .out1(Mask[1]), .out2(Mask[2]), .out3(Mask[3]), .sel(CurrentAddress_q[1:0]));  // open: en
  Demultiplexer #(.enable("false")) demultiplexer_3 (
    .out0(IncAddr), .out1(demultiplexer_3_out1), .in(demultiplexer_2_out1), .sel(End));
  Counter #(.width(4), .max('hf)) counter_1 (
    .load(Load), .D(WriteTime), .count(Write), .Q(counter_1_q), .clk(Clock));  // open: carry, clr
  Comparator #(.width(32)) comparator_1 (.a(Data), .b({32{1'b1}}), .eq(End));  // open: gt, lt
  Comparator #(.width(4)) comparator_2 (.a(4'b0000), .b(counter_1_q), .eq(WriteEnd));  // open: gt, lt

  // Other names for the same wires on the sheet: CLK = Clock; Count = Write; WT[3:0] = WriteTime
endmodule

// Mux
module MacroMUX (
  input  [31:0] Data_Input_8,
  input  [31:0] Data_Input_0,
  input  [31:0] Data_Input_9,
  input  [31:0] Data_Input_1,
  input  [31:0] Data_Input_10,
  input  [31:0] Data_Input_2,
  input  [31:0] Data_Input_11,
  input  [31:0] Data_Input_3,
  input  [31:0] Data_Input_12,
  input  [31:0] Data_Input_4,
  input  [31:0] Data_Input_13,
  input  [31:0] Data_Input_5,
  input  [31:0] Data_Input_14,
  input  [31:0] Data_Input_6,
  input  [31:0] Data_Input_15,
  input  [31:0] Data_Input_7,
  input  [31:0] Data_Input_16,
  input  [31:0] Data_Input_24,
  input  [31:0] Data_Input_17,
  input  [31:0] Data_Input_25,
  input  [31:0] Selector,
  input  [31:0] Data_Input_18,
  input  [31:0] Data_Input_26,
  input  [31:0] Data_Input_19,
  input  [31:0] Data_Input_27,
  input  [31:0] Data_Input_20,
  input  [31:0] Data_Input_28,
  input  [31:0] Data_Input_21,
  input  [31:0] Data_Input_29,
  input  [31:0] Data_Input_22,
  input  [31:0] Data_Input_30,
  input  [31:0] Data_Input_23,
  input  [31:0] Data_Input_31,
  output [31:0] Output
);

  wire undriven;
  wire [4:0] priority_encoder_1_out;

  Multiplexer #(.select(5), .width(32)) multiplexer_1 (
    .in0(Data_Input_0), .in1(Data_Input_1), .in2(Data_Input_2), .in3(Data_Input_3), .in4(Data_Input_4),
    .in5(Data_Input_5), .in6(Data_Input_6), .in7(Data_Input_7), .in8(Data_Input_8), .in9(Data_Input_9),
    .in10(Data_Input_10), .in11(Data_Input_11), .in12(Data_Input_12), .in13(Data_Input_13),
    .in14(Data_Input_14), .in15(Data_Input_15), .in16(Data_Input_16), .in17(Data_Input_17),
    .in18(Data_Input_18), .in19(Data_Input_19), .in20(Data_Input_20), .in21(Data_Input_21),
    .in22(Data_Input_22), .in23(Data_Input_23), .in24(Data_Input_24), .in25(Data_Input_25),
    .in26(Data_Input_26), .in27(Data_Input_27), .in28(Data_Input_28), .in29(Data_Input_29),
    .in30(Data_Input_30), .in31(Data_Input_31), .out(Output), .sel(priority_encoder_1_out), .en(undriven));
  Priority_Encoder #(.select(5), .disabled(0)) priority_encoder_1 (
    .in0(Selector[0]), .in1(Selector[1]), .in2(Selector[2]), .in3(Selector[3]), .in4(Selector[4]),
    .in5(Selector[5]), .in6(Selector[6]), .in7(Selector[7]), .in8(Selector[8]), .in9(Selector[9]),
    .in10(Selector[10]), .in11(Selector[11]), .in12(Selector[12]), .in13(Selector[13]), .in14(Selector[14]),
    .in15(Selector[15]), .in16(Selector[16]), .in17(Selector[17]), .in18(Selector[18]), .in19(Selector[19]),
    .in20(Selector[20]), .in21(Selector[21]), .in22(Selector[22]), .in23(Selector[23]), .in24(Selector[24]),
    .in25(Selector[25]), .in26(Selector[26]), .in27(Selector[27]), .in28(Selector[28]), .in29(Selector[29]),
    .in30(Selector[30]), .in31(Selector[31]), .out(priority_encoder_1_out));
endmodule

module Register_File (
  input  [31:0] Data_Input,
  input  Clock,
  input  RW,
  input  [4:0] Data_Address,
  input  Reset,
  input  HI___LO_enable,
  input  [31:0] HI_Input,
  input  [31:0] LO_Input,
  input  [4:0] Selector_A,
  input  [4:0] Selector_B,
  output [31:0] A,
  output [31:0] B,
  output [31:0] Hi_value,
  output [31:0] Lo_Value,
  output [31:0] SP
);

  wire _0, _1, _2, _3, _4, _5, _6, _7, _8, _9, _10, _11, _12, _13, _14, _15, _16, _17, _18, _19, _20, _21,
       _22, _23, _24, _25, _26, _27, _28, _29, _30, _31;
  wire [31:0] R0, R1, R2, R3, R4, R5, R6, R7, R8, R9, R10, R11, R12, R13, R14, R15, R16, R17, R18, R19, R20,
       R21, R22, R23, R24, R25, R26, R27, R28, R29, R30, SP_t;

  Hi hi_1 (.Input(HI_Input), .Enable(HI___LO_enable), .Output(Hi_value), .Clock(Clock));
  Lo lo_1 (.Input(LO_Input), .Enable(HI___LO_enable), .Clock(Clock), .Output(Lo_Value));
  Decoder #(.select(5)) decoder_1 (
    .out0(_0), .out1(_1), .out2(_2), .out3(_3), .out4(_4), .out5(_5), .out6(_6), .out7(_7), .out8(_8),
    .out9(_9), .out10(_10), .out11(_11), .out12(_12), .out13(_13), .out14(_14), .out15(_15), .out16(_16),
    .out17(_17), .out18(_18), .out19(_19), .out20(_20), .out21(_21), .out22(_22), .out23(_23), .out24(_24),
    .out25(_25), .out26(_26), .out27(_27), .out28(_28), .out29(_29), .out30(_30), .out31(_31),
    .sel(Data_Address), .en(RW));
  Register #(.width(32)) register_1 (.D(Data_Input), .en(_0), .Q(R0), .clk(Clock), .clr(1'b0));
  Register #(.width(32)) register_2 (.D(Data_Input), .en(_8), .Q(R8), .clk(Clock), .clr(Reset));
  Register #(.width(32)) register_3 (.D(Data_Input), .en(_16), .Q(R16), .clk(Clock), .clr(Reset));
  Register #(.width(32)) register_4 (.D(Data_Input), .en(_24), .Q(R24), .clk(Clock), .clr(Reset));
  Register #(.width(32)) register_5 (.D(Data_Input), .en(_1), .Q(R1), .clk(Clock), .clr(Reset));
  Register #(.width(32)) register_6 (.D(Data_Input), .en(_9), .Q(R9), .clk(Clock), .clr(Reset));
  Register #(.width(32)) register_7 (.D(Data_Input), .en(_17), .Q(R17), .clk(Clock), .clr(Reset));
  Register #(.width(32)) register_8 (.D(Data_Input), .en(_25), .Q(R25), .clk(Clock), .clr(Reset));
  Register #(.width(32)) register_9 (.D(Data_Input), .en(_2), .Q(R2), .clk(Clock), .clr(Reset));
  Register #(.width(32)) register_10 (.D(Data_Input), .en(_10), .Q(R10), .clk(Clock), .clr(Reset));
  Register #(.width(32)) register_11 (.D(Data_Input), .en(_18), .Q(R18), .clk(Clock), .clr(Reset));
  Register #(.width(32)) register_12 (.D(Data_Input), .en(_26), .Q(R26), .clk(Clock), .clr(Reset));
  Register #(.width(32)) register_13 (.D(Data_Input), .en(_3), .Q(R3), .clk(Clock), .clr(Reset));
  Register #(.width(32)) register_14 (.D(Data_Input), .en(_11), .Q(R11), .clk(Clock), .clr(Reset));
  Register #(.width(32)) register_15 (.D(Data_Input), .en(_19), .Q(R19), .clk(Clock), .clr(Reset));
  Register #(.width(32)) register_16 (.D(Data_Input), .en(_27), .Q(R27), .clk(Clock), .clr(Reset));
  Multiplexer #(.select(5), .width(32), .enable("false")) multiplexer_1 (
    .in0(R0), .in1(R1), .in2(R2), .in3(R3), .in4(R4), .in5(R5), .in6(R6), .in7(R7), .in8(R8), .in9(R9),
    .in10(R10), .in11(R11), .in12(R12), .in13(R13), .in14(R14), .in15(R15), .in16(R16), .in17(R17),
    .in18(R18), .in19(R19), .in20(R20), .in21(R21), .in22(R22), .in23(R23), .in24(R24), .in25(R25),
    .in26(R26), .in27(R27), .in28(R28), .in29(R29), .in30(R30), .in31(SP), .out(A), .sel(Selector_A));
  Register #(.width(32)) register_17 (.D(Data_Input), .en(_4), .Q(R4), .clk(Clock), .clr(Reset));
  Register #(.width(32)) register_18 (.D(Data_Input), .en(_12), .Q(R12), .clk(Clock), .clr(Reset));
  Register #(.width(32)) register_19 (.D(Data_Input), .en(_20), .Q(R20), .clk(Clock), .clr(Reset));
  Register #(.width(32)) register_20 (.D(Data_Input), .en(_28), .Q(R28), .clk(Clock), .clr(Reset));
  Register #(.width(32)) register_21 (.D(Data_Input), .en(_5), .Q(R5), .clk(Clock), .clr(Reset));
  Register #(.width(32)) register_22 (.D(Data_Input), .en(_13), .Q(R13), .clk(Clock), .clr(Reset));
  Register #(.width(32)) register_23 (.D(Data_Input), .en(_21), .Q(R21), .clk(Clock), .clr(Reset));
  Register #(.width(32)) register_24 (.D(Data_Input), .en(_29), .Q(R29), .clk(Clock), .clr(Reset));
  Register #(.width(32)) register_25 (.D(Data_Input), .en(_6), .Q(R6), .clk(Clock), .clr(Reset));
  Register #(.width(32)) register_26 (.D(Data_Input), .en(_14), .Q(R14), .clk(Clock), .clr(Reset));
  Register #(.width(32)) register_27 (.D(Data_Input), .en(_22), .Q(R22), .clk(Clock), .clr(Reset));
  Register #(.width(32)) register_28 (.D(Data_Input), .en(_30), .Q(R30), .clk(Clock), .clr(Reset));
  Register #(.width(32)) register_29 (.D(Data_Input), .en(_7), .Q(R7), .clk(Clock), .clr(Reset));
  Register #(.width(32)) register_30 (.D(Data_Input), .en(_15), .Q(R15), .clk(Clock), .clr(Reset));
  Register #(.width(32)) register_31 (.D(Data_Input), .en(_23), .Q(R23), .clk(Clock), .clr(Reset));
  Register #(.width(32)) register_32 (.D(SP_t), .en(_31), .Q(SP), .clk(Clock), .clr(Reset));
  Multiplexer #(.select(5), .width(32), .enable("false")) multiplexer_2 (
    .in0(R0), .in1(R1), .in2(R2), .in3(R3), .in4(R4), .in5(R5), .in6(R6), .in7(R7), .in8(R8), .in9(R9),
    .in10(R10), .in11(R11), .in12(R12), .in13(R13), .in14(R14), .in15(R15), .in16(R16), .in17(R17),
    .in18(R18), .in19(R19), .in20(R20), .in21(R21), .in22(R22), .in23(R23), .in24(R24), .in25(R25),
    .in26(R26), .in27(R27), .in28(R28), .in29(R29), .in30(R30), .in31(SP), .out(B), .sel(Selector_B));

  // Other names for the same wires on the sheet: DA[4:0] = Data_Address; Hi[31:0] = HI_Input;
  //   Hi___Lo = HI___LO_enable; Lo[31:0] = LO_Input; R31[31:0] = SP; Rst = Reset; Sa[4:0] = Selector_A;
  //   Sb[4:0] = Selector_B

  // Notes on the sheet:
  //   Entradas
  //   Hi / LO 
  //   0
  //   8
  //   16
  //   24
  //   1
  //   9
  //   17
  //   25
  //   2
  //   10
  //   18
  //   26
  //   3
  //   11
  //   19
  //   27
  //   Register File
  //   Registros
  //   Decodificador de la dirección
  //   4
  //   12
  //   20
  //   28
  //   Selectores de registros
  //   5
  //   13
  //   21
  //   29
  //   6
  //   14
  //   22
  //   30
  //   7
  //   15
  //   23
  //   31
  //   Leyenda
  //   Cada numero 
  //   representa su registro
  //   con su respectivo valor
  //   Salidas
endmodule

// ALU
module Arithmetic_Logic_Unit (
  input  [31:0] A,
  input  [31:0] B,
  input  [15:0] Constant,
  input  [31:0] Op,
  output [31:0] Value,
  output [31:0] Hi_Value,
  output [31:0] Lo_Value,
  output Hi___LO_was_used
);

  wire and_1_out, and_2_out, and_3_out, and_4_out;
  wire [0:0] c3;
  wire [1:0] MUX, not_3_out, not_4_out, not_5_out, not_6_out, O1, O2, O3, O4;
  wire [1:1] c2;
  wire [31:0] _0, _1, _2, _3, bit_extender_2_out, Lo_Value_t, Op1, Op2, Op3, Op4, Op5, Op6, Op7, Op8, Op9,
       Op10, Op11, Op12, Op13, Op14, Op15, Op16, Op17, Op18, Op21, Op30, Op31, Op32;

  not not_1 (c2[1], 1'b1);
  not not_2 (c3[0], 1'b1);
  and and_1 (and_1_out, Op[2], ~Op[3], ~Op[4], ~Op[5]);  // AND_Gate
  and and_2 (and_2_out, ~Op[2], Op[3], ~Op[4], ~Op[5]);  // AND_Gate
  and and_3 (and_3_out, ~Op[2], ~Op[3], Op[4], ~Op[5]);  // AND_Gate
  and and_4 (and_4_out, ~Op[2], ~Op[3], ~Op[4], Op[5]);  // AND_Gate
  assign Op21 = {{16{Constant[15]}}, Constant};  // Bit_Extender bit_extender_1
  assign bit_extender_2_out = {{16{1'b0}}, Constant};  // Bit_Extender bit_extender_2
  assign not_3_out = ~2'b11;  // NOT_Gate not_3, 2 bits wide
  Multiplexer #(.width(2)) multiplexer_1 (.in0(not_3_out), .in1(not_3_out), .out(O1), .sel(and_1_out));  // open: en
  assign not_4_out = ~2'b11;  // NOT_Gate not_4, 2 bits wide
  Multiplexer #(.width(2)) multiplexer_2 (.in0(not_4_out), .in1({c2[1], 1'b1}), .out(O2), .sel(and_2_out));  // open: en
  assign not_5_out = ~2'b11;  // NOT_Gate not_5, 2 bits wide
  Multiplexer #(.width(2)) multiplexer_3 (.in0(not_5_out), .in1({1'b1, c3[0]}), .out(O3), .sel(and_3_out));  // open: en
  assign not_6_out = ~2'b11;  // NOT_Gate not_6, 2 bits wide
  Multiplexer #(.width(2)) multiplexer_4 (.in0(not_6_out), .in1(2'b11), .out(O4), .sel(and_4_out));  // open: en
  Adder #(.width(32)) adder_1 (.a(A), .b(B), .out(Op1));  // open: cin, cout
  Subtractor #(.width(32)) subtractor_1 (.a(A), .b(B), .out(Op2));  // open: bin, bout
  Multiplier #(.width(32)) multiplier_1 (.a(A), .b(B), .out(Op3), .cout(_0));  // open: cin
  Unsigned_Mult unsigned_mult_1 (.in_1(A), .in_2(B), .Output(Op4), .Output_2(_1));
  Divider #(.width(32)) divider_1 (.a(A), .b(B), .out(Op5), .rem(_2));  // open: upper
  Unsigned_Div unsigned_div_1 (.in_1(A), .in_2(B), .Output(Op6), .Output_2(_3));
  Adder #(.width(32)) adder_2 (.a(A), .b(Op21), .out(Op7));  // open: cin, cout
  assign Op8 = A & B;  // AND_Gate And_5, 32 bits wide
  assign Op9 = A | B;  // OR_Gate Or, 32 bits wide
  assign Op10 = ~(A | B);  // NOR_Gate Nor, 32 bits wide
  assign Op11 = A ^ B;  // XOR_Gate Xor, 32 bits wide
  assign Op12 = A & bit_extender_2_out;  // AND_Gate Andi, 32 bits wide
  assign Op13 = A | bit_extender_2_out;  // OR_Gate Ori, 32 bits wide
  assign Op14 = A ^ bit_extender_2_out;  // XOR_Gate Xori, 32 bits wide
  Slt slt_1 (.Rs(A), .Rt(B), .Output(Op15));
  Unsigned_Slt unsigned_slt_1 (.Rs(A), .Rt(B), .Output(Op16));
  Slti slti_1 (.Rs(A), .Constant(Op21), .Output(Op17));
  Sltiu sltiu_1 (.Rs(A), .Constant(Op21), .Output(Op18));
  assign MUX = O1 | O2 | O3 | O4;  // OR_Gate or_2, 2 bits wide
  // Probe on MUX
  Multiplexer #(.select(2), .width(32)) multiplexer_5 (
    .in0(_0), .in1(_1), .in2(_2), .in3(_3), .out(Lo_Value_t), .sel(MUX));  // open: en
  or or_3 (Hi___LO_was_used, Op[2], Op[3], Op[4], Op[5]);
  MacroMUX macromux_1 (
    .Data_Input_8(Op9), .Data_Input_0(Op1), .Data_Input_9(Op10), .Data_Input_1(Op2), .Data_Input_10(Op11),
    .Data_Input_2(Op3), .Data_Input_11(Op12), .Data_Input_3(Op4), .Data_Input_12(Op13), .Data_Input_4(Op5),
    .Data_Input_13(Op14), .Data_Input_5(Op6), .Data_Input_14(Op15), .Data_Input_6(Op7), .Data_Input_15(Op16),
    .Data_Input_7(Op8), .Data_Input_16(Op17), .Data_Input_17(Op18), .Data_Input_18(Hi_Value),
    .Data_Input_19(Lo_Value), .Data_Input_20(Op21), .Data_Input_29(Op30), .Data_Input_30(Op31),
    .Data_Input_31(Op32), .Output(Value), .Selector(Op));  // open: Data_Input_24, Data_Input_25, Data_Input_26, Data_Input_27, Data_Input_28, Data_Input_21, Data_Input_22, Data_Input_23
  Hi hi_1 (.Input(Value), .Enable(Hi___LO_was_used), .Output(Hi_Value), .Clock(Hi___LO_was_used));
  Lo lo_1 (.Input(Lo_Value_t), .Enable(Hi___LO_was_used), .Clock(Hi___LO_was_used), .Output(Lo_Value));

  // Other names for the same wires on the sheet: C[15:0] = Constant; Hi___Lo = Hi___LO_was_used; a_t = Op[2];
  //   b_t = Op[3]; c_t = Op[4]; d = Op[5]; Hi[31:0] = Hi_Value; Op19[31:0] = Hi_Value; Lo[31:0] = Lo_Value;
  //   Op20[31:0] = Lo_Value; Out[31:0] = Value

  // Notes on the sheet:
  //   Entradas
  //   Lógica de guardado para registros Hi y LO
  //   Operaciones Aritmético-Logicas
  //   nop
  //   Selector de la operación
  //   Activador de Hi / Lo
  //   Salidas
endmodule

module Data_Path (
  input  Clock,
  input  RW,
  input  [4:0] DA,
  input  Rst,
  input  [4:0] SA,
  input  [4:0] SB,
  input  [31:0] Op,
  input  [15:0] Constant,
  input  [31:0] Inst,
  output [31:0] Output,
  output [31:0] A,
  output [31:0] B
);

  wire Hi___Lo;
  wire [31:0] Hi, Lo;

  Register_File register_file_1 (
    .Data_Input(Output), .A(A), .B(B), .RW(RW), .Data_Address(DA), .Reset(Rst), .Selector_A(SA),
    .Selector_B(SB), .Clock(Clock), .HI_Input(Hi), .LO_Input(Lo), .HI___LO_enable(Hi___Lo));  // open: Hi_value, Lo_Value, SP
  Arithmetic_Logic_Unit arithmetic_logic_unit_1 (
    .A(A), .B(B), .Constant(Constant), .Op(Op), .Hi_Value(Hi), .Lo_Value(Lo), .Hi___LO_was_used(Hi___Lo),
    .Value(Output));

  // Other names for the same wires on the sheet: Rs = Rst

  // Notes on the sheet:
  //   Entradas
  //   Data Path
  //   Salidas
endmodule

// ID
module Instruction_Decoder (
  input  W_Id,
  input  [31:0] Instruction,
  output R___W,
  output [31:0] Op,
  output [4:0] SA,
  output [4:0] SB,
  output [4:0] Data_Address,
  output [15:0] Constant,
  output Jmp,
  output S_Mult,
  output S_Div,
  output Memory
);

  wire O_Halt, O_Kbd, O_Rnd, O_Tty, R_Type;
  wire [4:0] not_1_out;
  wire [15:0] not_2_out;

  Sum_Bool sum_bool_1 (.in_1({Instruction[10:0], Instruction[31:26]}), .Output(Op[0]));
  Rest_Bool rest_bool_1 (.in_1({Instruction[10:0], Instruction[31:26]}), .Output(Op[1]));
  Mult_Bool mult_bool_1 (.in_1({Instruction[31:26], Instruction[15:0]}), .Output(Op[2]));
  MULU_bool mulu_bool_1 (.in_1({Instruction[31:26], Instruction[15:0]}), .Output(Op[3]));
  DIV_bool div_bool_1 (.in_1({Instruction[31:26], Instruction[15:0]}), .Output(Op[4]));
  Unsigned_Div_Bool unsigned_div_bool_1 (.in_1({Instruction[31:26], Instruction[15:0]}), .Output(Op[5]));
  Addi_Bool addi_bool_1 (.in_1(Instruction[31:26]), .Output(Op[6]));
  And_Bool and_bool_1 (
    .in_1({Instruction[10:3], Instruction[31], Instruction[2:0], Instruction[30:26]}), .Output(Op[7]));
  Or_Bool or_bool_1 (.in_1({Instruction[10:3], Instruction[31], Instruction[2:0], Instruction[30:26]}), .Output(Op[8]));
  Nor_Bool nor_bool_1 (
    .in_1({Instruction[10:3], Instruction[31], Instruction[2:0], Instruction[30:26]}), .Output(Op[9]));
  Xor_Bool xor_bool_1 (
    .in_1({Instruction[10:3], Instruction[31], Instruction[2:0], Instruction[30:26]}), .Output(Op[10]));
  Andi_Bool andi_bool_1 (.in_1(Instruction[31:26]), .Output(Op[11]));
  Ori_Bool ori_bool_1 (.in_1(Instruction[31:26]), .Output(Op[12]));
  Xori_Bool xori_bool_1 (.in_1(Instruction[31:26]), .Output(Op[13]));
  Slt_Bool slt_bool_1 (.in_1({Instruction[31:26], Instruction[15:0]}), .Output(Op[14]));
  Unsigned_Slt_Bool unsigned_slt_bool_1 (.in_1({Instruction[31:26], Instruction[15:0]}), .Output(Op[15]));
  Slti_Bool slti_bool_1 (.in_1(Instruction[31:26]), .Output(Op[16]));
  Sltiu_Bool sltiu_bool_1 (.in_1(Instruction[31:26]), .Output(Op[17]));
  Mfhi_Bool mfhi_bool_1 (.in_1({Instruction[31:16], Instruction[10:0]}), .Output(Op[18]));
  Mflo_Bool mflo_bool_1 (.in_1({Instruction[31:16], Instruction[10:0]}), .Output(Op[19]));
  nop nop_1 (.in_1({Instruction[15:11], Instruction[31:16], Instruction[10:0]}), .Output(Op[20]));
  Beq_Bool beq_bool_1 (.in_1(Instruction[31:26]), .Output(Op[21]));
  Bne_Bool bne_bool_1 (.in_1(Instruction[31:26]), .Output(Op[22]));
  Blez_Bool blez_bool_1 (.in_1(Instruction[31:26]), .Output(Op[23]));
  Bgtz_Bool bgtz_bool_1 (.in_1(Instruction[31:26]), .Output(Op[24]));
  Bltz_Bool bltz_bool_1 (.in_1(Instruction[31:26]), .Output(Op[25]));
  Jump_Bool jump_bool_1 (.in_1(Instruction[31:26]), .Output(Op[26]));
  Jr_Bool jr_bool_1 (.in_1({Instruction[31:26], Instruction[20:0]}), .Output(Op[27]));
  Lw_Bool lw_bool_1 (.Input(Instruction[31:26]), .Output(Op[28]));
  Sw_Bool sw_bool_1 (.Input(Instruction[31:26]), .Output(Op[29]));
  Pop_Bool pop_bool_1 (.Input({Instruction[31:16], Instruction[10:0]}), .Output(Op[30]));
  Push_Bool push_bool_1 (.Input({Instruction[31:26], Instruction[20:0]}), .Output(Op[31]));
  Halt_Bool halt_bool_1 (.in_1(Instruction), .Output(O_Halt));
  Tty_Bool tty_bool_1 (.in_1({Instruction[31:26], Instruction[20:0]}), .Output(O_Tty));
  Rnd_Bool rnd_bool_1 (.in_1({Instruction[31:16], Instruction[10:0]}), .Output(O_Rnd));
  Kbd_Bool kbd_bool_1 (.in_1({Instruction[31:16], Instruction[10:0]}), .Output(O_Kbd));
  assign not_1_out = ~{5{1'b1}};  // NOT_Gate not_1, 5 bits wide
  assign not_2_out = ~{16{1'b1}};  // NOT_Gate not_2, 16 bits wide
  or or_1 (S_Mult, Op[3], Op[2]);
  or or_2 (S_Div, Op[4], Op[5]);
  Multiplexer #(.width(5), .enable("false")) multiplexer_1 (
    .in0(Instruction[25:21]), .in1(Instruction[20:16]), .out(SA), .sel(R_Type));
  Multiplexer #(.width(5), .enable("false")) multiplexer_2 (
    .in0(not_1_out), .in1(Instruction[25:21]), .out(SB), .sel(R_Type));
  Multiplexer #(.width(5), .enable("false")) multiplexer_3 (
    .in0(Instruction[20:16]), .in1(Instruction[15:11]), .out(Data_Address), .sel(R_Type));
  Multiplexer #(.width(16), .enable("false")) multiplexer_4 (
    .in0(Instruction[15:0]), .in1(not_2_out), .out(Constant), .sel(R_Type));
  or or_3 (R_Type, Op[0], Op[1], Op[2], Op[3], Op[4], Op[5], Op[30], Op[7], Op[8], Op[9], Op[10], Op[15], Op[14]);
  or or_4 (Jmp, Op[21], Op[22], Op[23], Op[24], Op[26], Op[27], Op[25], Op[28], Op[29], Op[30], Op[31]);
  or or_5 (Memory, Op[29], Op[28], Op[30], Op[31]);
  not not_3 (R___W, Jmp);

  // Other names for the same wires on the sheet: d5[4:0] = Instruction[25:21];
  //   G27[26:0] = {Instruction[31:16], Instruction[10:0]}; Inst[31:0] = Instruction; c5[4:0] = Instruction[20:16];
  //   H27[26:0] = {Instruction[31:26], Instruction[20:0]}; e6[5:0] = Instruction[31:26];
  //   f17[16:0] = {Instruction[10:0], Instruction[31:26]}; a11[10:0] = Instruction[10:0];
  //   b5[4:0] = Instruction[15:11]; DA[4:0] = Data_Address; Mm = Memory; O__plus = Op[0]; O__minus = Op[1];
  //   O__star = Op[2]; O__star_star = Op[3]; O = Op[4]; O_t = Op[5]; O__plus_plus = Op[6]; O_And = Op[7];
  //   O_Or = Op[8]; O_Nor = Op[9]; O_Xor = Op[10]; O_Andi = Op[11]; O_Ori = Op[12]; O_Xori = Op[13]; O_Slt = Op[14];
  //   O_U_Slt = Op[15]; O_Slti = Op[16]; O_Sltiu = Op[17]; O_Mfhi = Op[18]; O_Mflo = Op[19]; O_Nop = Op[20];
  //   O_Beq = Op[21]; O_Bne = Op[22]; O_Blez = Op[23]; O_Bgtz = Op[24]; O_Bltz = Op[25]; O_Jump = Op[26];
  //   O_Jr = Op[27]; O_Lw = Op[28]; O_Sw = Op[29]; O_Pop = Op[30]; O_Push = Op[31]

  // Notes on the sheet:
  //   Entradas y bits usados por separado
  //   Decodificador de operación
  //   Instruction Decoder
  //   Unificador de encendido o apagado
  //   de las operaciones
  //   Hi /Lo Verificator
  //   Selector de Registros
  //   Selector de Constante
  //   Selector de Tipo de operación
  //   Revisar los jumps ,me falta 1
  //   Salidas
  //   Son más casos de RW
endmodule

// Bc
module Branch_Control (
  input  [31:0] Inst,
  input  [31:0] A,
  input  [31:0] B,
  input  [15:0] Js,
  input  [31:0] Op,
  input  [31:0] Pc,
  input  Clock,
  input  Jump,
  output [31:0] PC_prime
);

  wire [25:0] bitselector_1_out;
  wire [31:0] Beq, Bgtz, Blez, Bltz, Bne, Jump_Register, Jump_t, Load_Word;

  Beq beq_1 (.A(A), .B(B), .PC(Pc), .Js(Js), .PC_prime(Beq));
  Bltz bltz_1 (.A(A), .PC(Pc), .Js(Js), .PC_prime(Bltz));
  BitSelector #(.width(32), .group(26)) bitselector_1 (.in(Inst), .out(bitselector_1_out), .sel(1'b0));
  Bne bne_1 (.A(A), .B(B), .PC(Pc), .Js(Js), .PC_prime(Bne));
  Jump jump_1 (.in_1(bitselector_1_out), .PC(Pc), .Js(Js), .Pc_prime(Jump_t));
  MacroMUX macromux_1 (
    .Data_Input_24(Bgtz), .Data_Input_25(Bltz), .Data_Input_26(Jump_t), .Data_Input_27(Jump_Register),
    .Data_Input_28(Load_Word), .Data_Input_21(Beq), .Data_Input_22(Bne), .Data_Input_23(Blez),
    .Output(PC_prime), .Selector(Op));  // open: Data_Input_8, Data_Input_0, Data_Input_9, Data_Input_1, Data_Input_10, Data_Input_2, Data_Input_11, Data_Input_3, Data_Input_12, Data_Input_4, Data_Input_13, Data_Input_5, Data_Input_14, Data_Input_6, Data_Input_15, Data_Input_7, Data_Input_16, Data_Input_17, Data_Input_18, Data_Input_19, Data_Input_20, Data_Input_29, Data_Input_30, Data_Input_31
  Jr jr_1 (.A(A), .PC_prime(Jump_Register));
  Blez blez_1 (.A(A), .PC(Pc), .Js(Js), .PC_prime(Blez));
  Bgtz bgtz_1 (.A(A), .PC(Pc), .Js(Js), .PC_prime(Bgtz));

  // Other names for the same wires on the sheet: Jmp = Jump
endmodule

// C2
module PC_Sumer (
  input  [31:0] Input,
  output [31:0] Sum
);

  wire [2:2] not_2_out;
  wire [15:0] not_1_out;
  wire [31:0] bit_extender_1_out;

  assign not_1_out = ~{16{1'b1}};  // NOT_Gate not_1, 16 bits wide
  not not_2 (not_2_out[2], not_1_out[2]);
  assign bit_extender_1_out = {{16{1'b0}}, {not_1_out[15:3], not_2_out[2], not_1_out[1:0]}};  // Bit_Extender bit_extender_1
  Adder #(.width(32)) adder_1 (.a(Input), .b(bit_extender_1_out), .out(Sum));  // open: cin, cout

  // Notes on the sheet:
  //   Sumador del PC por defecto (sumar 4)
endmodule

// PC
module PC_3_0 (
  input  Clock_1,
  input  Clock_2,
  input  Rst,
  input  [31:0] ADDR,
  input  [31:0] PC_prime_input,
  input  Jmp,
  output [31:0] PC,
  output [31:0] PC_prime
);

  wire counter_1_q;
  wire [31:0] multiplexer_1_out, multiplexer_2_out, pc_sumer_1_sum;

  Counter #(.width(1), .max('h1), .ongoal("stay")) counter_1 (
    .Q(counter_1_q), .clk(Clock_1), .clr(Rst));  // open: load, D, count, carry
  Multiplexer #(.width(32), .enable("false")) multiplexer_1 (
    .in0(ADDR), .in1(PC_prime), .out(multiplexer_1_out), .sel(counter_1_q));
  // Probe on PC
  Register #(.width(32)) Dir_1 (.D(multiplexer_1_out), .Q(PC), .clk(Clock_1), .clr(Rst));  // open: en
  PC_Sumer pc_sumer_1 (.Input(PC), .Sum(pc_sumer_1_sum));
  Multiplexer #(.width(32)) multiplexer_2 (
    .in0(pc_sumer_1_sum), .in1(PC_prime_input), .out(multiplexer_2_out), .sel(Jmp));  // open: en
  Register #(.width(32)) Dir_2 (.D(multiplexer_2_out), .Q(PC_prime), .clk(Clock_2), .clr(Rst));  // open: en

  // Notes on the sheet:
  //   Program Counter 
endmodule

// HI
module Hi (
  input  [31:0] Input,
  input  Enable,
  input  Clock,
  output [31:0] Output
);

  Register #(.width(32)) register_1 (.D(Input), .en(Enable), .Q(Output), .clk(Clock));  // open: clr
endmodule

// LO
module Lo (
  input  [31:0] Input,
  input  Enable,
  input  Clock,
  output [31:0] Output
);

  Register #(.width(32)) register_1 (.D(Input), .en(Enable), .Q(Output), .clk(Clock));  // open: clr
endmodule

// +
module Sum_Bool (
  input  [16:0] in_1,
  output Output
);

  wire not_1_out, not_2_out, not_3_out, not_4_out, not_5_out, not_6_out, not_7_out, not_8_out, not_9_out,
       not_10_out, not_11_out, not_12_out, not_13_out, not_14_out, not_15_out, not_16_out;

  not not_1 (not_1_out, in_1[0]);
  not not_2 (not_2_out, in_1[1]);
  not not_3 (not_3_out, in_1[2]);
  not not_4 (not_4_out, in_1[3]);
  not not_5 (not_5_out, in_1[4]);
  not not_6 (not_6_out, in_1[5]);
  not not_7 (not_7_out, in_1[6]);
  not not_8 (not_8_out, in_1[7]);
  and and_1 (Output, not_1_out, not_2_out, not_3_out, not_4_out, not_5_out, not_6_out, not_7_out, not_8_out, not_9_out, not_10_out, not_11_out, in_1[11], not_12_out, not_13_out, not_14_out, not_15_out, not_16_out);
  not not_9 (not_9_out, in_1[8]);
  not not_10 (not_10_out, in_1[9]);
  not not_11 (not_11_out, in_1[10]);
  not not_12 (not_12_out, in_1[12]);
  not not_13 (not_13_out, in_1[13]);
  not not_14 (not_14_out, in_1[14]);
  not not_15 (not_15_out, in_1[15]);
  not not_16 (not_16_out, in_1[16]);
endmodule

// -
module Rest_Bool (
  input  [16:0] in_1,
  output Output
);

  and and_1 (Output, ~in_1[0], ~in_1[1], ~in_1[2], ~in_1[3], ~in_1[4], ~in_1[5], ~in_1[6], in_1[7], ~in_1[8], ~in_1[9], ~in_1[10], in_1[11], ~in_1[12], ~in_1[13], ~in_1[14], ~in_1[15], ~in_1[16]);  // AND_Gate
endmodule

// *
module Mult_Bool (
  input  [21:0] in_1,
  output Output
);

  wire not_1_out, not_2_out, or_1_out, or_2_out;

  or or_1 (or_1_out, in_1[0], in_1[1], in_1[2], ~in_1[3], ~in_1[4], in_1[5]);  // OR_Gate
  not not_1 (not_1_out, or_1_out);
  or or_2 (or_2_out, in_1[6], in_1[7], in_1[8], in_1[9], in_1[10], in_1[11], in_1[12], in_1[13], in_1[14], in_1[15], in_1[16], in_1[17], in_1[18], in_1[19], in_1[20], in_1[21]);
  not not_2 (not_2_out, or_2_out);
  and and_1 (Output, not_1_out, not_2_out);
endmodule

// **
module MULU_bool (
  input  [21:0] in_1,
  output Output
);

  wire not_1_out, not_2_out, or_1_out, or_2_out;

  not not_1 (not_1_out, or_1_out);
  or or_1 (or_1_out, ~in_1[0], in_1[1], in_1[2], ~in_1[3], ~in_1[4], in_1[5]);  // OR_Gate
  not not_2 (not_2_out, or_2_out);
  or or_2 (or_2_out, in_1[6], in_1[7], in_1[8], in_1[9], in_1[10], in_1[11], in_1[12], in_1[13], in_1[14], in_1[15], in_1[16], in_1[17], in_1[18], in_1[19], in_1[20], in_1[21]);
  and and_1 (Output, not_1_out, not_2_out);
endmodule

// /
module DIV_bool (
  input  [21:0] in_1,
  output Output
);

  wire not_1_out, not_2_out, or_1_out, or_2_out;

  or or_1 (or_1_out, in_1[0], ~in_1[1], in_1[2], ~in_1[3], ~in_1[4], in_1[5]);  // OR_Gate
  not not_1 (not_1_out, or_1_out);
  or or_2 (or_2_out, in_1[6], in_1[7], in_1[8], in_1[9], in_1[10], in_1[11], in_1[12], in_1[13], in_1[14], in_1[15], in_1[16], in_1[17], in_1[18], in_1[19], in_1[20], in_1[21]);
  not not_2 (not_2_out, or_2_out);
  and and_1 (Output, not_1_out, not_2_out);
endmodule

// //
module Unsigned_Div_Bool (
  input  [21:0] in_1,
  output Output
);

  wire not_1_out, not_2_out, or_1_out, or_2_out;

  or or_1 (or_1_out, ~in_1[0], ~in_1[1], in_1[2], ~in_1[3], ~in_1[4], in_1[5]);  // OR_Gate
  not not_1 (not_1_out, or_1_out);
  not not_2 (not_2_out, or_2_out);
  or or_2 (or_2_out, in_1[6], in_1[7], in_1[8], in_1[9], in_1[10], in_1[11], in_1[12], in_1[13], in_1[14], in_1[15], in_1[16], in_1[17], in_1[18], in_1[19], in_1[20], in_1[21]);
  and and_1 (Output, not_1_out, not_2_out);
endmodule

// ++
module Addi_Bool (
  input  [5:0] in_1,
  output Output
);

  wire or_1_out;

  not not_1 (Output, or_1_out);
  or or_1 (or_1_out, in_1[0], in_1[1], in_1[2], ~in_1[3], in_1[4], in_1[5]);  // OR_Gate
endmodule

// And
module And_Bool (
  input  [16:0] in_1,
  output Output
);

  wire or_1_out;

  or or_1 (or_1_out, in_1[0], in_1[1], in_1[2], in_1[3], in_1[4], in_1[5], in_1[6], ~in_1[7], in_1[8], in_1[9], in_1[10], ~in_1[11], in_1[12], in_1[13], in_1[14], in_1[15], in_1[16]);  // OR_Gate
  not not_1 (Output, or_1_out);
endmodule

// Or
module Or_Bool (
  input  [16:0] in_1,
  output Output
);

  wire or_1_out;

  or or_1 (or_1_out, in_1[0], in_1[1], in_1[2], in_1[3], in_1[4], ~in_1[5], in_1[6], ~in_1[7], in_1[8], in_1[9], in_1[10], ~in_1[11], in_1[12], in_1[13], in_1[14], in_1[15], in_1[16]);  // OR_Gate
  not not_1 (Output, or_1_out);
endmodule

// Nor
module Nor_Bool (
  input  [16:0] in_1,
  output Output
);

  wire or_1_out;

  not not_1 (Output, or_1_out);
  or or_1 (or_1_out, in_1[0], in_1[1], in_1[2], in_1[3], in_1[4], ~in_1[5], ~in_1[6], ~in_1[7], in_1[8], in_1[9], in_1[10], ~in_1[11], in_1[12], in_1[13], in_1[14], in_1[15], in_1[16]);  // OR_Gate
endmodule

// Xor
module Xor_Bool (
  input  [16:0] in_1,
  output Output
);

  wire or_1_out;

  or or_1 (or_1_out, in_1[0], in_1[1], in_1[2], in_1[3], in_1[4], in_1[5], in_1[6], in_1[7], in_1[8], ~in_1[9], in_1[10], ~in_1[11], in_1[12], in_1[13], in_1[14], in_1[15], in_1[16]);  // OR_Gate
  not not_1 (Output, or_1_out);
endmodule

// Andi
module Andi_Bool (
  input  [5:0] in_1,
  output Output
);

  wire or_1_out;

  or or_1 (or_1_out, in_1[0], in_1[1], ~in_1[2], ~in_1[3], in_1[4], in_1[5]);  // OR_Gate
  not not_1 (Output, or_1_out);
endmodule

// Ori
module Ori_Bool (
  input  [5:0] in_1,
  output Output
);

  wire or_1_out;

  or or_1 (or_1_out, ~in_1[0], in_1[1], ~in_1[2], ~in_1[3], in_1[4], in_1[5]);  // OR_Gate
  not not_1 (Output, or_1_out);
endmodule

// Xori
module Xori_Bool (
  input  [5:0] in_1,
  output Output
);

  wire or_1_out;

  or or_1 (or_1_out, in_1[0], ~in_1[1], ~in_1[2], ~in_1[3], in_1[4], in_1[5]);  // OR_Gate
  not not_1 (Output, or_1_out);
endmodule

// Slt
module Slt_Bool (
  input  [21:0] in_1,
  output Output
);

  wire or_1_out;

  or or_1 (or_1_out, in_1[0], ~in_1[1], in_1[2], ~in_1[3], in_1[4], ~in_1[5], in_1[6], in_1[7], in_1[8], in_1[9], in_1[10], in_1[12], in_1[13], in_1[14], in_1[15], in_1[16], in_1[17], in_1[18], in_1[19], in_1[20], in_1[21], in_1[11]);  // OR_Gate
  not not_1 (Output, or_1_out);
endmodule

// U/Slt
module Unsigned_Slt_Bool (
  input  [21:0] in_1,
  output Output
);

  wire or_1_out;

  or or_1 (or_1_out, ~in_1[0], ~in_1[1], in_1[2], ~in_1[3], in_1[4], ~in_1[5], in_1[6], in_1[7], in_1[8], in_1[9], in_1[10], in_1[12], in_1[13], in_1[14], in_1[15], in_1[16], in_1[17], in_1[18], in_1[19], in_1[20], in_1[21], in_1[11]);  // OR_Gate
  not not_1 (Output, or_1_out);
endmodule

// Slti
module Slti_Bool (
  input  [5:0] in_1,
  output Output
);

  wire or_1_out;

  or or_1 (or_1_out, in_1[0], ~in_1[1], in_1[2], in_1[4], in_1[5], ~in_1[3]);  // OR_Gate
  not not_1 (Output, or_1_out);
endmodule

// Sltiu
module Sltiu_Bool (
  input  [5:0] in_1,
  output Output
);

  wire or_1_out;

  or or_1 (or_1_out, ~in_1[0], ~in_1[1], in_1[2], in_1[4], in_1[5], ~in_1[3]);  // OR_Gate
  not not_1 (Output, or_1_out);
endmodule

// Mfhi
module Mfhi_Bool (
  input  [26:0] in_1,
  output Output
);

  wire or_1_out;

  or or_1 (or_1_out, in_1[0], in_1[1], in_1[2], in_1[3], ~in_1[4], in_1[5], in_1[6], in_1[7], in_1[8], in_1[9], in_1[10], in_1[11], in_1[12], in_1[13], in_1[14], in_1[15], in_1[16], in_1[17], in_1[18], in_1[19], in_1[20], in_1[21], in_1[22], in_1[23], in_1[24], in_1[25], in_1[26]);  // OR_Gate
  not not_1 (Output, or_1_out);
endmodule

// Mflo
module Mflo_Bool (
  input  [26:0] in_1,
  output Output
);

  wire or_1_out;

  or or_1 (or_1_out, in_1[0], ~in_1[1], in_1[2], in_1[3], ~in_1[4], in_1[5], in_1[6], in_1[7], in_1[8], in_1[9], in_1[10], in_1[11], in_1[12], in_1[13], in_1[14], in_1[15], in_1[16], in_1[17], in_1[18], in_1[19], in_1[20], in_1[21], in_1[22], in_1[23], in_1[24], in_1[25], in_1[26]);  // OR_Gate
  not not_1 (Output, or_1_out);
endmodule

// Beq
module Beq_Bool (
  input  [5:0] in_1,
  output Output
);

  wire or_1_out;

  or or_1 (or_1_out, in_1[0], in_1[1], ~in_1[2], in_1[4], in_1[5], in_1[3]);  // OR_Gate
  not not_1 (Output, or_1_out);
endmodule

// Bne
module Bne_bool (
  input  [5:0] in_1,
  output Output
);

  wire or_1_out;

  or or_1 (or_1_out, ~in_1[0], in_1[1], ~in_1[2], in_1[4], in_1[5], in_1[3]);  // OR_Gate
  not not_1 (Output, or_1_out);
endmodule

// Bne
module Bne_Bool (
  input  [5:0] in_1,
  output Output
);

  wire or_1_out;

  or or_1 (or_1_out, ~in_1[0], in_1[1], ~in_1[2], in_1[4], in_1[5], in_1[3]);  // OR_Gate
  not not_1 (Output, or_1_out);
endmodule

// Blez
module Blez_Bool (
  input  [5:0] in_1,
  output Output
);

  wire or_1_out;

  or or_1 (or_1_out, in_1[0], ~in_1[1], ~in_1[2], in_1[4], in_1[5], in_1[3]);  // OR_Gate
  not not_1 (Output, or_1_out);
endmodule

// Bgtz
module Bgtz_Bool (
  input  [5:0] in_1,
  output Output
);

  wire or_1_out;

  or or_1 (or_1_out, ~in_1[0], ~in_1[1], ~in_1[2], in_1[4], in_1[5], in_1[3]);  // OR_Gate
  not not_1 (Output, or_1_out);
endmodule

// Bltz
module Bltz_Bool (
  input  [5:0] in_1,
  output Output
);

  wire or_1_out;

  or or_1 (or_1_out, ~in_1[0], in_1[1], in_1[2], in_1[4], in_1[5], in_1[3]);  // OR_Gate
  not not_1 (Output, or_1_out);
endmodule

// Jump
module Jump_Bool (
  input  [5:0] in_1,
  output Output
);

  wire or_1_out;

  or or_1 (or_1_out, in_1[0], ~in_1[1], in_1[2], in_1[4], in_1[5], in_1[3]);  // OR_Gate
  not not_1 (Output, or_1_out);
endmodule

// Jr
module Jr_Bool (
  input  [26:0] in_1,
  output Output
);

  wire or_1_out;

  or or_1 (or_1_out, in_1[0], in_1[1], in_1[2], ~in_1[3], in_1[4], in_1[5], in_1[6], in_1[7], in_1[8], in_1[9], in_1[10], in_1[11], in_1[12], in_1[13], in_1[14], in_1[15], in_1[16], in_1[17], in_1[18], in_1[19], in_1[20], in_1[21], in_1[22], in_1[23], in_1[24], in_1[25], in_1[26]);  // OR_Gate
  not not_1 (Output, or_1_out);
endmodule

// Mult
module Unsigned_Mult (
  input  [31:0] in_1,
  input  [31:0] in_2,
  output [31:0] Output,
  output [31:0] Output_2
);

  wire [31:0] complemento_a_2_1_output, complemento_a_2_2_output, multiplexer_1_out, multiplexer_2_out;

  Complemento_a_2 complemento_a_2_1 (.Input(in_1), .Output(complemento_a_2_1_output));
  Complemento_a_2 complemento_a_2_2 (.Input(in_2), .Output(complemento_a_2_2_output));
  Multiplexer #(.width(32)) multiplexer_1 (
    .in0(in_1), .in1(complemento_a_2_1_output), .out(multiplexer_1_out), .sel(in_1[31]));  // open: en
  Multiplexer #(.width(32)) multiplexer_2 (
    .in0(in_2), .in1(complemento_a_2_2_output), .out(multiplexer_2_out), .sel(in_2[31]));  // open: en
  Multiplier #(.width(32)) multiplier_1 (
    .a(multiplexer_1_out), .b(multiplexer_2_out), .out(Output), .cout(Output_2));  // open: cin

  // Notes on the sheet:
  //   Multiplicador Sin Signo
endmodule

// Div
module Unsigned_Div (
  input  [31:0] in_1,
  input  [31:0] in_2,
  output [31:0] Output,
  output [31:0] Output_2
);

  wire [31:0] complemento_a_2_1_output, complemento_a_2_2_output, multiplexer_1_out, multiplexer_2_out;

  Complemento_a_2 complemento_a_2_1 (.Input(in_1), .Output(complemento_a_2_1_output));
  Complemento_a_2 complemento_a_2_2 (.Input(in_2), .Output(complemento_a_2_2_output));
  Multiplexer #(.width(32)) multiplexer_1 (
    .in0(in_1), .in1(complemento_a_2_1_output), .out(multiplexer_1_out), .sel(in_1[31]));  // open: en
  Multiplexer #(.width(32)) multiplexer_2 (
    .in0(in_2), .in1(complemento_a_2_2_output), .out(multiplexer_2_out), .sel(in_2[31]));  // open: en
  Divider #(.width(32)) divider_1 (
    .a(multiplexer_1_out), .b(multiplexer_2_out), .out(Output), .rem(Output_2));  // open: upper

  // Notes on the sheet:
  //   Divisor sin signo
endmodule

module Slt (
  input  [31:0] Rs,
  input  [31:0] Rt,
  output [31:0] Output
);

  wire comparator_1_lt;
  wire [0:0] not_16_out;
  wire [15:0] multiplexer_1_out;
  wire [15:1] not_1_out;

  not not_1 (not_1_out[1], 1'b1);
  not not_2 (not_1_out[2], 1'b1);
  not not_3 (not_1_out[3], 1'b1);
  not not_4 (not_1_out[4], 1'b1);
  not not_5 (not_1_out[5], 1'b1);
  not not_6 (not_1_out[6], 1'b1);
  not not_7 (not_1_out[7], 1'b1);
  not not_8 (not_1_out[8], 1'b1);
  not not_9 (not_1_out[9], 1'b1);
  not not_10 (not_1_out[10], 1'b1);
  not not_11 (not_1_out[11], 1'b1);
  not not_12 (not_1_out[12], 1'b1);
  not not_13 (not_1_out[13], 1'b1);
  not not_14 (not_1_out[14], 1'b1);
  not not_15 (not_1_out[15], 1'b1);
  Comparator #(.width(32)) comparator_1 (.a(Rs), .b(Rt), .lt(comparator_1_lt));  // open: gt, eq
  not not_16 (not_16_out[0], 1'b1);
  Multiplexer #(.width(16)) multiplexer_1 (
    .in0({not_1_out, not_16_out[0]}), .in1({not_1_out, 1'b1}), .out(multiplexer_1_out), .sel(comparator_1_lt));  // open: en
  assign Output = {{16{1'b0}}, multiplexer_1_out};  // Bit_Extender bit_extender_1

  // Notes on the sheet:
  //   Comparador de registros
endmodule

module Slti (
  input  [31:0] Rs,
  input  [31:0] Constant,
  output [31:0] Output
);

  wire comparator_1_lt;
  wire [0:0] not_16_out;
  wire [15:0] multiplexer_1_out;
  wire [15:1] not_1_out;

  not not_1 (not_1_out[1], 1'b1);
  not not_2 (not_1_out[2], 1'b1);
  not not_3 (not_1_out[3], 1'b1);
  not not_4 (not_1_out[4], 1'b1);
  not not_5 (not_1_out[5], 1'b1);
  not not_6 (not_1_out[6], 1'b1);
  not not_7 (not_1_out[7], 1'b1);
  not not_8 (not_1_out[8], 1'b1);
  not not_9 (not_1_out[9], 1'b1);
  not not_10 (not_1_out[10], 1'b1);
  not not_11 (not_1_out[11], 1'b1);
  not not_12 (not_1_out[12], 1'b1);
  not not_13 (not_1_out[13], 1'b1);
  not not_14 (not_1_out[14], 1'b1);
  not not_15 (not_1_out[15], 1'b1);
  not not_16 (not_16_out[0], 1'b1);
  Comparator #(.width(32)) comparator_1 (.a(Rs), .b(Constant), .lt(comparator_1_lt));  // open: gt, eq
  Multiplexer #(.width(16)) multiplexer_1 (
    .in0({not_1_out, not_16_out[0]}), .in1({not_1_out, 1'b1}), .out(multiplexer_1_out), .sel(comparator_1_lt));  // open: en
  assign Output = {{16{1'b0}}, multiplexer_1_out};  // Bit_Extender bit_extender_1

  // Notes on the sheet:
  //   Comparador de registros
endmodule

module Sltiu (
  input  [31:0] Rs,
  input  [31:0] Constant,
  output [31:0] Output
);

  wire comparator_1_lt;
  wire [0:0] not_16_out;
  wire [15:0] multiplexer_1_out;
  wire [15:1] not_1_out;

  not not_1 (not_1_out[1], 1'b1);
  not not_2 (not_1_out[2], 1'b1);
  not not_3 (not_1_out[3], 1'b1);
  not not_4 (not_1_out[4], 1'b1);
  not not_5 (not_1_out[5], 1'b1);
  not not_6 (not_1_out[6], 1'b1);
  not not_7 (not_1_out[7], 1'b1);
  not not_8 (not_1_out[8], 1'b1);
  not not_9 (not_1_out[9], 1'b1);
  not not_10 (not_1_out[10], 1'b1);
  not not_11 (not_1_out[11], 1'b1);
  not not_12 (not_1_out[12], 1'b1);
  not not_13 (not_1_out[13], 1'b1);
  not not_14 (not_1_out[14], 1'b1);
  not not_15 (not_1_out[15], 1'b1);
  not not_16 (not_16_out[0], 1'b1);
  Comparator #(.width(32), .mode("unsigned")) comparator_1 (
    .a(Rs), .b(Constant), .lt(comparator_1_lt));  // open: gt, eq
  Multiplexer #(.width(16)) multiplexer_1 (
    .in0({not_1_out, not_16_out[0]}), .in1({not_1_out, 1'b1}), .out(multiplexer_1_out), .sel(comparator_1_lt));  // open: en
  assign Output = {{16{1'b0}}, multiplexer_1_out};  // Bit_Extender bit_extender_1

  // Notes on the sheet:
  //   Comparador de registros
endmodule

// U / Slt
module Unsigned_Slt (
  input  [31:0] Rs,
  input  [31:0] Rt,
  output [31:0] Output
);

  wire comparator_1_lt;
  wire [0:0] not_16_out;
  wire [15:0] multiplexer_1_out;
  wire [15:1] not_1_out;

  not not_1 (not_1_out[1], 1'b1);
  not not_2 (not_1_out[2], 1'b1);
  not not_3 (not_1_out[3], 1'b1);
  not not_4 (not_1_out[4], 1'b1);
  not not_5 (not_1_out[5], 1'b1);
  not not_6 (not_1_out[6], 1'b1);
  not not_7 (not_1_out[7], 1'b1);
  not not_8 (not_1_out[8], 1'b1);
  not not_9 (not_1_out[9], 1'b1);
  not not_10 (not_1_out[10], 1'b1);
  not not_11 (not_1_out[11], 1'b1);
  not not_12 (not_1_out[12], 1'b1);
  not not_13 (not_1_out[13], 1'b1);
  not not_14 (not_1_out[14], 1'b1);
  not not_15 (not_1_out[15], 1'b1);
  not not_16 (not_16_out[0], 1'b1);
  Comparator #(.width(32), .mode("unsigned")) comparator_1 (.a(Rs), .b(Rt), .lt(comparator_1_lt));  // open: gt, eq
  Multiplexer #(.width(16)) multiplexer_1 (
    .in0({not_1_out, not_16_out[0]}), .in1({not_1_out, 1'b1}), .out(multiplexer_1_out), .sel(comparator_1_lt));  // open: en
  assign Output = {{16{1'b0}}, multiplexer_1_out};  // Bit_Extender bit_extender_1

  // Notes on the sheet:
  //   Comparador sin signo
endmodule

// C2
module Complemento_a_2 (
  input  [31:0] Input,
  output [31:0] Output
);

  wire [31:0] bit_extender_1_out, not_1_out;

  assign not_1_out = ~Input;  // NOT_Gate not_1, 32 bits wide
  assign bit_extender_1_out = {{31{1'b0}}, 1'b1};  // Bit_Extender bit_extender_1
  // Probe on bit_extender_1_out
  Adder #(.width(32)) adder_1 (.a(not_1_out), .b(bit_extender_1_out), .out(Output));  // open: cin, cout
endmodule

// Nop
module nop (
  input  [31:0] in_1,
  output Output
);

  wire or_1_out;

  or or_1 (or_1_out, in_1[0], in_1[1], in_1[2], in_1[3], in_1[4], in_1[5], in_1[6], in_1[7], in_1[8], in_1[9], in_1[10], in_1[11], in_1[12], in_1[13], in_1[14], in_1[15], in_1[17], in_1[18], in_1[19], in_1[20], in_1[21], in_1[22], in_1[23], in_1[24], in_1[25], in_1[26], in_1[27], in_1[28], in_1[29], in_1[30], in_1[31], in_1[16]);
  not not_1 (Output, or_1_out);
endmodule

module Beq (
  input  [31:0] A,
  input  [31:0] B,
  input  [31:0] PC,
  input  [15:0] Js,
  output [31:0] PC_prime
);

  wire comparator_1_eq;
  wire [2:2] not_1_out;
  wire [31:0] _4, adder_1_out, S1, S2;
  wire [31:18] Sum;

  assign {_4[31:3], not_1_out[2], _4[1:0]} = ~{32{1'b1}};  // NOT_Gate not_1, 32 bits wide
  not not_2 (_4[2], not_1_out[2]);
  assign Sum = {{13{Js[15]}}, Js[15]};  // Bit_Extender bit_extender_1
  Comparator #(.width(32)) comparator_1 (.a(A), .b(B), .eq(comparator_1_eq));  // open: gt, lt
  Multiplexer #(.width(32)) multiplexer_1 (.in0(S1), .in1(S2), .out(PC_prime), .sel(comparator_1_eq));  // open: en
  Adder #(.width(32)) adder_1 (.a(PC), .b({Sum, Js, 2'b00}), .out(adder_1_out));  // open: cin, cout
  Adder #(.width(32)) adder_2 (.a(PC), .b(_4), .out(S1));  // open: cin, cout
  Adder #(.width(32)) adder_3 (.a(adder_1_out), .b(_4), .out(S2));  // open: cin, cout

  // Other names for the same wires on the sheet: Sum[17:2] = Js
endmodule

module Bne (
  input  [31:0] A,
  input  [31:0] B,
  input  [31:0] PC,
  input  [15:0] Js,
  output [31:0] PC_prime
);

  wire comparator_1_eq;
  wire [2:2] not_1_out;
  wire [31:0] _4, adder_1_out, S1, S2;
  wire [31:18] Sum;

  assign {_4[31:3], not_1_out[2], _4[1:0]} = ~{32{1'b1}};  // NOT_Gate not_1, 32 bits wide
  not not_2 (_4[2], not_1_out[2]);
  assign Sum = {{13{Js[15]}}, Js[15]};  // Bit_Extender bit_extender_1
  Comparator #(.width(32)) comparator_1 (.a(A), .b(B), .eq(comparator_1_eq));  // open: gt, lt
  Multiplexer #(.width(32)) multiplexer_1 (.in0(S2), .in1(S1), .out(PC_prime), .sel(comparator_1_eq));  // open: en
  Adder #(.width(32)) adder_1 (.a(PC), .b({Sum, Js, 2'b00}), .out(adder_1_out));  // open: cin, cout
  Adder #(.width(32)) adder_2 (.a(PC), .b(_4), .out(S1));  // open: cin, cout
  Adder #(.width(32)) adder_3 (.a(adder_1_out), .b(_4), .out(S2));  // open: cin, cout

  // Other names for the same wires on the sheet: Sum[17:2] = Js
endmodule

module Blez (
  input  [31:0] A,
  input  [31:0] PC,
  input  [15:0] Js,
  output [31:0] PC_prime
);

  wire comparator_1_gt;
  wire [2:2] not_1_out;
  wire [31:0] _4, adder_1_out, S1, S2;
  wire [31:18] Sum;

  assign {_4[31:3], not_1_out[2], _4[1:0]} = ~{32{1'b1}};  // NOT_Gate not_1, 32 bits wide
  not not_2 (_4[2], not_1_out[2]);
  assign Sum = {{13{Js[15]}}, Js[15]};  // Bit_Extender bit_extender_1
  Comparator #(.width(32)) comparator_1 (.a(A), .b({32{1'b0}}), .gt(comparator_1_gt));  // open: eq, lt
  Multiplexer #(.width(32)) multiplexer_1 (.in0(S2), .in1(S1), .out(PC_prime), .sel(comparator_1_gt));  // open: en
  Adder #(.width(32)) adder_1 (.a(PC), .b({Sum, Js, 2'b00}), .out(adder_1_out));  // open: cin, cout
  Adder #(.width(32)) adder_2 (.a(PC), .b(_4), .out(S1));  // open: cin, cout
  Adder #(.width(32)) adder_3 (.a(adder_1_out), .b(_4), .out(S2));  // open: cin, cout

  // Other names for the same wires on the sheet: Sum[17:2] = Js
endmodule

module Bgtz (
  input  [31:0] A,
  input  [31:0] PC,
  input  [15:0] Js,
  output [31:0] PC_prime
);

  wire comparator_1_gt;
  wire [2:2] not_1_out;
  wire [31:0] _4, adder_1_out, S1, S2;
  wire [31:18] Sum;

  assign {_4[31:3], not_1_out[2], _4[1:0]} = ~{32{1'b1}};  // NOT_Gate not_1, 32 bits wide
  not not_2 (_4[2], not_1_out[2]);
  assign Sum = {{13{Js[15]}}, Js[15]};  // Bit_Extender bit_extender_1
  Comparator #(.width(32)) comparator_1 (.a(A), .b({32{1'b0}}), .gt(comparator_1_gt));  // open: eq, lt
  Multiplexer #(.width(32)) multiplexer_1 (.in0(S1), .in1(S2), .out(PC_prime), .sel(comparator_1_gt));  // open: en
  Adder #(.width(32)) adder_1 (.a(PC), .b({Sum, Js, 2'b00}), .out(adder_1_out));  // open: cin, cout
  Adder #(.width(32)) adder_2 (.a(PC), .b(_4), .out(S1));  // open: cin, cout
  Adder #(.width(32)) adder_3 (.a(adder_1_out), .b(_4), .out(S2));  // open: cin, cout

  // Other names for the same wires on the sheet: Sum[17:2] = Js
endmodule

module Bltz (
  input  [31:0] A,
  input  [31:0] PC,
  input  [15:0] Js,
  output [31:0] PC_prime
);

  wire comparator_1_lt;
  wire [2:2] not_1_out;
  wire [31:0] _4, adder_1_out, S1, S2;
  wire [31:18] Sum;

  assign {_4[31:3], not_1_out[2], _4[1:0]} = ~{32{1'b1}};  // NOT_Gate not_1, 32 bits wide
  not not_2 (_4[2], not_1_out[2]);
  assign Sum = {{13{Js[15]}}, Js[15]};  // Bit_Extender bit_extender_1
  Comparator #(.width(32)) comparator_1 (.a(A), .b({32{1'b0}}), .lt(comparator_1_lt));  // open: gt, eq
  Multiplexer #(.width(32)) multiplexer_1 (.in0(S1), .in1(S2), .out(PC_prime), .sel(comparator_1_lt));  // open: en
  Adder #(.width(32)) adder_1 (.a(PC), .b({Sum, Js, 2'b00}), .out(adder_1_out));  // open: cin, cout
  Adder #(.width(32)) adder_2 (.a(PC), .b(_4), .out(S1));  // open: cin, cout
  Adder #(.width(32)) adder_3 (.a(adder_1_out), .b(_4), .out(S2));  // open: cin, cout

  // Other names for the same wires on the sheet: Sum[17:2] = Js
endmodule

module Jump (
  input  [25:0] in_1,
  input  [31:0] PC,
  input  [15:0] Js,
  output [31:0] Pc_prime
);

  wire [2:2] not_1_out;
  wire [31:0] _4;

  assign {_4[31:3], not_1_out[2], _4[1:0]} = ~{32{1'b1}};  // NOT_Gate not_1, 32 bits wide
  not not_2 (_4[2], not_1_out[2]);
  BitSelector #(.width(32), .group(4)) bitselector_1 (.in(PC), .out(Pc_prime[31:28]), .sel(3'b111));

  assign Pc_prime[27:0] = {in_1, 2'b00};

  // Other names for the same wires on the sheet: Input[25:0] = in_1
endmodule

module Jr (
  input  [31:0] A,
  output [31:0] PC_prime
);


  assign PC_prime = A;
endmodule

// Lw
module Lw_Bool (
  input  [5:0] Input,
  output Output
);

  wire or_1_out;

  or or_1 (or_1_out, ~Input[0], ~Input[1], Input[2], Input[4], ~Input[5], Input[3]);  // OR_Gate
  not not_1 (Output, or_1_out);
endmodule

// Sw
module Sw_Bool (
  input  [5:0] Input,
  output Output
);

  wire or_1_out;

  or or_1 (or_1_out, ~Input[0], ~Input[1], Input[2], Input[4], ~Input[5], ~Input[3]);  // OR_Gate
  not not_1 (Output, or_1_out);
endmodule

// Pop
module Pop_Bool (
  input  [26:0] Input,
  output Output
);

  wire or_1_out;

  or or_1 (or_1_out, Input[0], Input[1], Input[2], Input[3], Input[4], Input[5], Input[6], Input[7], Input[8], Input[9], Input[10], Input[11], Input[12], Input[13], Input[14], Input[15], Input[16], Input[17], Input[18], Input[19], Input[20], Input[21], Input[22], Input[23], ~Input[24], ~Input[25], ~Input[26]);  // OR_Gate
  not not_1 (Output, or_1_out);
endmodule

// Push
module Push_Bool (
  input  [26:0] Input,
  output Output
);

  wire or_1_out;

  or or_1 (or_1_out, ~Input[0], Input[1], Input[2], Input[3], Input[4], Input[5], Input[6], Input[7], Input[8], Input[9], Input[10], Input[11], Input[12], Input[13], Input[14], Input[15], Input[16], Input[17], Input[18], Input[19], Input[20], Input[21], Input[22], Input[23], ~Input[24], ~Input[25], ~Input[26]);  // OR_Gate
  not not_1 (Output, or_1_out);

  // Notes on the sheet:
  //   No son los mismos bits que el pop ,se usa otro registro
endmodule

// Halt
module Halt_Bool (
  input  [31:0] in_1,
  output Output
);

  wire or_1_out;

  or or_1 (or_1_out, ~in_1[0], ~in_1[1], ~in_1[2], ~in_1[3], ~in_1[4], ~in_1[5], in_1[6], in_1[7], in_1[8], in_1[9], in_1[10], in_1[11], in_1[12], in_1[13], in_1[14], in_1[15], in_1[17], in_1[18], in_1[19], in_1[20], in_1[21], in_1[22], in_1[23], in_1[24], in_1[25], ~in_1[26], ~in_1[27], ~in_1[28], ~in_1[29], ~in_1[30], ~in_1[31], in_1[16]);  // OR_Gate
  not not_1 (Output, or_1_out);
endmodule

// Tty
module Tty_Bool (
  input  [26:0] in_1,
  output Output
);

  wire or_1_out;

  or or_1 (or_1_out, ~in_1[0], in_1[1], in_1[2], in_1[3], in_1[4], in_1[5], in_1[6], in_1[7], in_1[8], in_1[9], in_1[10], in_1[11], in_1[12], in_1[13], in_1[14], in_1[15], in_1[16], in_1[17], in_1[18], in_1[19], in_1[20], ~in_1[21], ~in_1[22], ~in_1[23], ~in_1[24], ~in_1[25], ~in_1[26]);  // OR_Gate
  not not_1 (Output, or_1_out);
endmodule

// Rnd
module Rnd_Bool (
  input  [26:0] in_1,
  output Output
);

  wire or_1_out;

  or or_1 (or_1_out, in_1[0], ~in_1[1], in_1[2], in_1[3], in_1[4], in_1[5], in_1[6], in_1[7], in_1[8], in_1[9], in_1[10], in_1[11], in_1[12], in_1[13], in_1[14], in_1[15], in_1[16], in_1[17], in_1[18], in_1[19], in_1[20], ~in_1[21], ~in_1[22], ~in_1[23], ~in_1[24], ~in_1[25], ~in_1[26]);  // OR_Gate
  not not_1 (Output, or_1_out);
endmodule

// Kbd
module Kbd_Bool (
  input  [26:0] in_1,
  output Output
);

  wire or_1_out;

  or or_1 (or_1_out, in_1[0], in_1[1], ~in_1[2], in_1[3], in_1[4], in_1[5], in_1[6], in_1[7], in_1[8], in_1[9], in_1[10], in_1[11], in_1[12], in_1[13], in_1[14], in_1[15], in_1[16], in_1[17], in_1[18], in_1[19], in_1[20], ~in_1[21], ~in_1[22], ~in_1[23], ~in_1[24], ~in_1[25], ~in_1[26]);  // OR_Gate
  not not_1 (Output, or_1_out);
endmodule

module Lw (
  input  [31:0] Last_Operation,
  input  Clock,
  input  Jmp,
  input  Clear,
  input  [31:0] A,
  input  [31:0] Jz,
  output [31:0] Last_Operation_2,
  output Counter,
  output [31:0] Value
);

  wire counter_1_q, not_1_out;
  wire [31:0] adder_1_out;

  Counter #(.width(1), .max('h1), .ongoal("stay")) counter_1 (
    .Q(counter_1_q), .clk(Clock), .clr(not_1_out));  // open: load, D, count, carry
  not not_1 (not_1_out, Jmp);
  Register #(.width(32), .trigger("falling")) register_1 (
    .D(Last_Operation), .en(counter_1_q), .Q(Last_Operation_2), .clk(Clock));  // open: clr
  Adder #(.width(32)) adder_1 (.a(A), .b(Jz), .out(adder_1_out));  // open: cin, cout
  Counter #(.width(1), .max('h1), .ongoal("stay")) counter_2 (
    .Q(Counter), .clk(Jmp), .clr(Clear));  // open: load, D, count, carry
  Register #(.width(32), .trigger("falling")) register_2 (
    .D(adder_1_out), .en(counter_1_q), .Q(Value), .clk(Clock));  // open: clr
endmodule

// I
module Inversor (
  input  [31:0] in_1,
  output [31:0] out_2
);


  assign out_2 = {in_1[7:0], in_1[15:8], in_1[23:16], in_1[31:24]};
endmodule
